# Fritzing sketch ImageSynth (saved by Fritzing 1.0.2b)
breadboards: 1

parts:
  S1 = SWITCH-MOMENTARY-2 [package=tactile_switch_smd]
  S2 = SWITCH-MOMENTARY-2 [package=tactile_switch_smd]
  S3 = SWITCH-MOMENTARY-2 [package=tactile_switch_smd]
  S4 = SWITCH-MOMENTARY-2 [package=tactile_switch_smd]
  S5 = SWITCH-MOMENTARY-2 [package=tactile_switch_smd]
  Part1 = Arduino Uno (Rev3) - ICSP
  RHT1 = Humidity and Temperature Sensor RHT03
  R1 = Resistor [tolerance=±5% resistance=220 package="0402 [SMD]"]
  R2 = Resistor [tolerance=±5% resistance=220 package="0402 [SMD]"]
  R3 = Resistor [tolerance=±5% resistance=220 package="0402 [SMD]"]
  R4 = Resistor [tolerance=±5% resistance=220 package="0402 [SMD]"]
  R5 = Resistor [tolerance=±5% resistance=220 package="0402 [SMD]"]

nets:
  5V: S1.1, S2.1, S3.1, S4.1, S5.1, Part1.5V, RHT1.Vcc
  N1: S1.2, Part1.D7
  N2: S2.2, Part1.D6_PWM
  N3: S3.2, Part1.D5_PWM
  N4: S4.2, Part1.D4
  N5: S5.2, Part1.D3_PWM
  N6: Part1.D2, RHT1.Data-signal
  N7: Part1.GND, RHT1.GND_1, R1.Pin_1, R2.Pin_1, R3.Pin_1, R4.Pin_1, R5.Pin_1
